# Fritzing sketch breadboard-layout (saved by Fritzing 0.9.3b)
breadboards: 1

parts:
  부품1 = orange board (Rev3)
  J1 = Piezo Speaker
  J2 = Basic Servo
  J3 = Basic Servo
  POT2 = Breadboard Trimpot
  DHT1 = DHT11 Humitidy and Temperature Sensor
  S1 = Reed switch [package=THT]
  R1 = Resistor [tolerance=±5% resistance=220 package=THT]
  Water_Level_Sensor1 = Water Level Sensor
  C1 = Electrolytic Capacitor [capacitance=1µF package="100 mil [THT, electrolytic]"]
  R2 = Resistor [tolerance=±5% resistance=220 package=THT]

nets:
  N1: 부품1.A0, POT2.PIN2
  N2: 부품1.A1, DHT1.NULL
  N3: 부품1.A2, Water_Level_Sensor1.SIG
  N4: 부품1.D9_PWM, J2.pulse
  GND: 부품1.GND, J1.pin1, J2.gnd, J3.gnd, POT2.PIN3, DHT1.GND, S1.pin_1, R1.Pin_0, R1.Pin_1, Water_Level_Sensor1.GND, R2.Pin_0
  N5: 부품1.D6_PWM, J3.pulse
  VCC: 부품1.5V, J1.pin2, J2.vcc, J3.vcc, POT2.PIN1, DHT1.VDD, S1.pin_2, Water_Level_Sensor1.VCC, C1.-
  N6: C1.+, R2.Pin_1

custom parts:
  orange board (Rev3): The orange board is a microcontroller board based on the ATmega328 (datasheet). It has 14 digital input/output pins (of which 6 can be used as PWM outputs), 6 analog inputs, a 16 MHz ceramic resonator, a USB connection, a power jack, an ICSP header, and a reset button. It contains everything needed to support the microcontroller; simply connect it to a computer with a USB cable or power it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
  DHT11 Humitidy and Temperature Sensor: DHT11 Humidity and Temperature Sensor
  Water Level Sensor: A water level sensor. This sensor operates at 3V to 5V. The Sig (signal) pin outputs an analogue signal that is in proportion to the amount of water in contact with the sensor.
